# Fritzing sketch ActivityIndicator (saved by Fritzing 0.9.5d)
breadboards: 1

parts:
  Q1 = NPN-Transistor [package="TO92 [THT]"]
  R1 = Resistor [tolerance=±5% resistance=1k package=THT]
  R2 = Resistor [tolerance=±5% resistance=1k package=THT]
  LED1 = LED - 5mm [color="Red (633nm)" package="5 mm [THT]"]
  U1 = RJ45 Jack [package=rj45-8]
  R3 = Resistor [tolerance=±5% resistance=1k package=THT]

nets:
  GND: Q1.E, U1.6
  N1: Q1.B, R2.Pin_0, R3.Pin_0
  N2: Q1.C, R1.Pin_1, LED1.anode
  5V: R1.Pin_0
  N3: R2.Pin_1, U1.2
  N4: LED1.cathode, R3.Pin_1
