# Fritzing sketch RemoteControl (saved by Fritzing 0.9.5d)
breadboards: 1

parts:
  Компонент1 = Arduino Nano (Rev3.0)
  U1 = Sharp PC817 [package=THT]
  U2 = Sharp PC817 [package=THT]
  U3 = Sharp PC817 [package=THT]
  U4 = Sharp PC817 [package=THT]
  R1 = Resistor [tolerance=±5% resistance=220 package=THT]
  R2 = Resistor [tolerance=±5% resistance=220 package=THT]
  R3 = Resistor [tolerance=±5% resistance=220 package=THT]
  R4 = Resistor [tolerance=±5% resistance=220 package=THT]
  Main_Selector = Rotary Encoder [package=THT]
  Confirm_Key_(Menu) = Pushbutton [package="[THT]"]
  Exit/ABCD = Pushbutton [package="[THT]"]
  R5 = Resistor [tolerance=±5% resistance=1k package=THT]
  U5 = RJ45 Jack [package=rj45-8]
  Q1 = MOSFET-NCHANNEL [package=to-92]
  R6 = Resistor [tolerance=±5% resistance=1k package=THT]
  R7 = Resistor [tolerance=±5% resistance=1k package=THT]

nets:
  GND: Компонент1.GND, U1.Pin_2, U2.Pin_2, U3.Pin_2, U4.Pin_2, U5.6, Q1.S, R7.Pin_1
  N1: Компонент1.D3, R5.Pin_0
  N2: Компонент1.D6, R4.Pin_1
  N3: Компонент1.D8, R3.Pin_1
  N4: Компонент1.D9, R6.Pin_0
  N5: Компонент1.D10, R2.Pin_1
  N6: Компонент1.D12/MISO, R1.Pin_1
  N7: U1.Pin_1, R1.Pin_0
  N8: U1.Pin_4, Main_Selector.EncoderPinB
  N9: U1.Pin_3, U2.Pin_3, Main_Selector.EncoderPinC
  N10: U2.Pin_1, R2.Pin_0
  N11: U2.Pin_4, Main_Selector.EncoderPinA
  N12: U3.Pin_1, R3.Pin_0
  N13: U3.Pin_4, Confirm_Key_(Menu).Pin_3, Confirm_Key_(Menu).Pin_4
  N14: U3.Pin_3, Confirm_Key_(Menu).Pin_1, Confirm_Key_(Menu).Pin_2
  N15: U4.Pin_1, R4.Pin_0
  N16: U4.Pin_4, Exit/ABCD.Pin_3, Exit/ABCD.Pin_4
  N17: U4.Pin_3, Exit/ABCD.Pin_1, Exit/ABCD.Pin_2
  N18: R5.Pin_1, U5.2
  N19: U5.8, Q1.D
  N20: Q1.G, R6.Pin_1, R7.Pin_0
